# Fritzing sketch CYD - Batten Lights with Switches (saved by Fritzing 1.0.4)
perfboards: 1

parts:
  M1 = RioRand LM2596
  S1 = Adafruit 3104 lighted pushbutton [package=THT]
  J1 = female pin header, 2 pins [form="♀ (female)"]
  J2 = female pin header, 2 pins [form="♀ (female)"]
  A35 = SMD2835 24V LED Strip
  A36 = SMD2835 24V LED Strip
  A37 = SMD2835 24V LED Strip
  A38 = SMD2835 24V LED Strip
  A39 = SMD2835 24V LED Strip
  A40 = SMD2835 24V LED Strip
  A41 = SMD2835 24V LED Strip
  A42 = SMD2835 24V LED Strip
  J3 = female pin header, 2 pins [form="♀ (female)"]  # not connected
  J4 = female pin header, 2 pins [form="♀ (female)"]
  A43 = SMD2835 24V LED Strip
  A44 = SMD2835 24V LED Strip
  A45 = SMD2835 24V LED Strip
  A46 = SMD2835 24V LED Strip
  A47 = SMD2835 24V LED Strip
  A48 = SMD2835 24V LED Strip
  A49 = SMD2835 24V LED Strip
  A50 = SMD2835 24V LED Strip
  Ground_Rail = Camdenboss CTB0158-10 [part_number=CTB0158-10 package=THT]
  PS1 = prefix0000 [part_number=S-350-60]
  J5 = Camdenboss CTB0158-3 [part_number=CTB0158-3 package=THT]  # not connected
  J6 = Camdenboss CTB0158-3 [part_number=CTB0158-3 package=THT]
  A51 = ESP32-2432S028R
  M3 = xy-mos d4184 [package=THT]
  Ground_Rail1 = Camdenboss CTB0158-3 [part_number=CTB0158-3 package=THT]
  R5 = Resistor [tolerance=±5% power=0.25W resistance=10k package=THT]
  S7 = Pushbutton [package=THT]
  C8 = Ceramic Capacitor [capacitance=100nF voltage=35V package="100 mil [THT, multilayer]"]
  C7 = Ceramic Capacitor [capacitance=100nF voltage=35V package="100 mil [THT, multilayer]"]
  S5 = Pushbutton [package=THT]
  S6 = Pushbutton [package=THT]
  C9 = Ceramic Capacitor [capacitance=100nF voltage=35V package="100 mil [THT, multilayer]"]
  R6 = Resistor [tolerance=±5% power=0.25W resistance=10k package=THT]
  R7 = Resistor [tolerance=±5% power=0.25W resistance=10k package=THT]

nets:
  N1: M1.Pin_1, Ground_Rail1.terminal_2
  N2: M1.Pin_2, Ground_Rail.terminal_5
  N3: M1.Pin_3, A51.Pin_12
  N4: M1.Pin_4, A51.Pin_1, A51.Pin_5, A51.Pin_9, S7.leg1, S5.leg1
  N5: S1.pin_5, S1.pin_4, Ground_Rail1.terminal_1
  N6: S1.pin_6, PS1.connector2
  N7: J1.pin1, J2.pin1, A35.+24V#1, A35.GND#3, A36.+24V#1, A36.GND#3, A37.GND#0, A37.+24V#2, A38.GND#0, A38.+24V#2, A39.GND#0, A39.+24V#2, A40.GND#0, A40.+24V#2, A41.+24V#1, A41.GND#3, A42.+24V#1, A42.GND#3, J4.pin1, A43.+24V#1, A43.GND#3, A44.+24V#1, A44.GND#3, A45.+24V#1, A45.GND#3, A46.+24V#1, A46.GND#3, A47.GND#0, A47.+24V#2, A48.GND#0, A48.+24V#2, A49.GND#0, A49.+24V#2, A50.GND#0, A50.+24V#2, M3.pin10
  N8: J1.pin2, J2.pin2, A35.GND#0, A35.+24V#2, A36.GND#0, A36.+24V#2, A37.+24V#1, A37.GND#3, A38.+24V#1, A38.GND#3, A39.+24V#1, A39.GND#3, A40.+24V#1, A40.GND#3, A41.GND#0, A41.+24V#2, A42.GND#0, A42.+24V#2, J4.pin2, A43.GND#0, A43.+24V#2, A44.GND#0, A44.+24V#2, A45.GND#0, A45.+24V#2, A46.GND#0, A46.+24V#2, A47.+24V#1, A47.GND#3, A48.+24V#1, A48.GND#3, A49.+24V#1, A49.GND#3, A50.+24V#1, A50.GND#3, M3.pin9
  N9: Ground_Rail.terminal_8, M3.pin2, M3.pin3, M3.pin4, M3.pin7
  N10: Ground_Rail.terminal_9, PS1.connector4
  N11: PS1.connector6, J6.terminal_3
  N12: PS1.connector7, J6.terminal_2
  N13: PS1.connector8, J6.terminal_1
  N14: A51.Pin_2, C7.1, S5.leg0, R7.Pin_1
  N15: A51.Pin_3, S7.leg0, C8.1, R6.Pin_1
  N16: A51.Pin_7, R5.Pin_1, S6.leg0, C9.1
  N17: A51.Pin_8, R5.Pin_0
  N18: M3.pin8, Ground_Rail1.terminal_3

notes:
  18 AWG Wire
  CYAN - 24+
  BROWN - Ground
  ================
  24 AWG
  RED - +
  BLACK - Ground
  5V
  Live, Neutral, Earth
  Australian 240V Power Cable
  Standard since 2003
  GND (bridge)
  GPIO 35 (UP)
  GPIO 22 (DOWN)
  GPIO 21 X UNUSED
  (remove from connector)
  GND
  GPIO 22(duplicate)
  GPIO 27 (SWITCH)
  3.3v
  GPIO 25
  LED PWM Output
  From Chip (disables touch)
  SMD2835 LEDS
  Light
  10k resistor between 3.3v and one side of switch
  100nf capacitor between same side and ground
  gpio from same side
  ground from other side
  < > OK
  +VIN
  -VIN
  +OUT
  -OUT

custom parts:
  Adafruit 3104 lighted pushbutton: This Mini Illuminated Momentary Power Button it an adorable breadboard-friendly tactile switch that has a built-in LED. It provides a simple way to add a tactile switch and a colorful universal power symbol to your project.
  SMD2835 24V LED Strip: 24V SMD2835 LED Strip
  ESP32-2432S028R: The ESP32-2432S028R development board.
  xy-mos d4184: xy-mos d4184 Two parallel N-Channel logic compatible MOSFETS with low Rds(on) for high current low-side switching applications.
